# Fritzing sketch nas-projekt (saved by Fritzing 0.9.2b)
breadboards: 1

parts:
  Part1 = Arduino Uno (Rev3)
  S2 = Momentary Switch [package=ksa_sealed_tac_switch]
  S1 = Momentary Switch [package=ksa_sealed_tac_switch]
  Grove1 = Grove 4 Digit Display
  Grove2 = Grove 4 Digit Display
  Grove3 = Grove 4 Digit Display

nets:
  N1: Part1.D8, S2.3
  N2: Part1.D9_PWM, S1.3
  N3: Part1.D2, Grove1.DIO
  N4: Part1.D3_PWM, Grove1.CLK
  N5: Part1.D4, Grove2.DIO
  N6: Part1.D5_PWM, Grove2.CLK
  N7: Part1.D6_PWM, Grove3.DIO
  N8: Part1.D7, Grove3.CLK
  VCC: Part1.5V, Grove1.VCC, Grove2.VCC, Grove3.VCC
  GND: Part1.GND, S2.1, S1.1, Grove1.GND, Grove2.GND, Grove3.GND
